// Logisim project MyCPU.circ as structural Verilog: 2 circuits, main circuit main
module main (
  input  in_1,
  input  in_2,
  output out_3
);

  and and_1 (out_3, in_1, in_2);
  Transistor transistor_1 ();  // open: in, out, gate
endmodule

module ULA (
  input  [15:0] A,
  input  [15:0] B,
  input  [3:0] op,
  output out_4
);

  Adder adder_1 (.a(A[7:0]), .b(B[7:0]));  // open: out, cin, cout
  // Pins of 1 and 8 and 16 bits meet at B
  // Pins of 1 and 8 and 16 bits meet at A
endmodule
